// Logisim project dom_zad_2_git.circ as structural Verilog: 1 circuit, main circuit NOR_birthdate
module NOR_birthdate (
  input  A,
  input  B,
  input  C,
  input  D,
  input  E,
  output Y
);

  wire nor_1_out, nor_2_out, nor_3_out, nor_4_out, nor_5_out, nor_6_out, nor_7_out, nor_8_out;

  nor nor_1 (nor_1_out, B, B);
  nor nor_2 (nor_2_out, E, E);
  nor nor_3 (nor_3_out, D, nor_2_out);
  nor nor_4 (nor_4_out, nor_1_out, C);
  nor nor_5 (nor_5_out, nor_4_out, nor_4_out);
  nor nor_6 (nor_6_out, nor_3_out, nor_3_out);
  nor nor_7 (nor_7_out, nor_5_out, nor_6_out);
  nor nor_8 (nor_8_out, nor_7_out, nor_7_out);
  nor nor_9 (Y, A, nor_8_out);

  // Notes on the sheet:
  //   25.02
  //   Uros Kostic
  //   FINK SI
  //   589/2015
  //   2+5+0+2= 9
  //   9=01001
endmodule
