// Logisim project domacizad.circ as structural Verilog: 1 circuit, main circuit domaci log kolo
module domaci_log_kolo (
  input  x1,
  input  x2,
  input  x3,
  input  x4,
  input  x5,
  input  x6,
  input  x7,
  input  x8,
  output Y
);

  wire and_1_out, and_2_out, and_4_out, not_1_out, not_2_out, not_3_out, or_1_out;

  not not_1 (not_1_out, x1);
  and and_1 (and_1_out, not_1_out, x2);
  not not_2 (not_2_out, x3);
  and and_2 (and_2_out, not_2_out, x4);
  or or_1 (or_1_out, and_1_out, and_2_out, and_4_out);
  and and_3 (Y, x7, or_1_out, x8);
  not not_3 (not_3_out, x5);
  and and_4 (and_4_out, not_3_out, x6);
endmodule
